// Logisim project automatic_street_light.circ as structural Verilog: 1 circuit, main circuit main
module main (
  input  D_DAYLIGHT,
  input  M_MANUAL_OVERRIDE,
  input  E_SYSTEM_ENABLE,
  output L_STREET_LIGHT
);

  wire or_1_p1, or_1_p3;

  // NOT_Gate not_1 has open pins: in=D_DAYLIGHT, out=open
  // OR_Gate or_1: pin names not known; wires that end beside it: or_1_p1, M_MANUAL_OVERRIDE, or_1_p3
  // AND_Gate and_1 has open pins: in0=or_1_p3, in1=E_SYSTEM_ENABLE, out=open
  LED STREET_LIGHT_LED ();  // open: in
endmodule
